// Logisim project g1.circ as structural Verilog: 13 circuits, main circuit 4-bit ALU
module _1_bit_sum (
  input  cin,
  input  a,
  input  b,
  output out_4
);

  wire and_1_out, and_2_out, and_3_out, and_4_out;

  and and_1 (and_1_out, ~cin, a, ~b);  // AND_Gate
  and and_2 (and_2_out, ~cin, ~a, b);  // AND_Gate
  and and_3 (and_3_out, cin, ~a, ~b);  // AND_Gate
  and and_4 (and_4_out, cin, a, b);
  or or_1 (out_4, and_1_out, and_2_out, and_3_out, and_4_out);
endmodule

module _1_bit_carryout (
  input  cin,
  input  a,
  input  b,
  output out_4
);

  wire and_1_out, and_2_out, and_3_out;

  and and_1 (and_1_out, cin, a);
  and and_2 (and_2_out, cin, b);
  and and_3 (and_3_out, a, b);
  or or_1 (out_4, and_1_out, and_2_out, and_3_out);
endmodule

module _1_bit_full_adder (
  input  cin,
  input  a,
  input  b,
  output sum,
  output cout
);

  _1_bit_sum u_1_bit_sum_1 (.cin(cin), .a(a), .b(b), .out_4(sum));
  _1_bit_carryout u_1_bit_carryout_1 (.cin(cin), .a(a), .b(b), .out_4(cout));
endmodule

module _1_bit_ALU (
  input  ainvert,
  input  binvert,
  input  cin,
  input  [1:0] op,
  input  a,
  input  b,
  input  less,
  output result,
  output cout
);

  wire and_1_out, multiplexer_1_out, multiplexer_2_out, n1_bit_full_adder_1_sum, not_1_out, not_2_out,
       or_1_out;

  Multiplexer multiplexer_1 (.in0(a), .in1(not_1_out), .out(multiplexer_1_out), .sel(ainvert));
  not not_1 (not_1_out, a);
  not not_2 (not_2_out, b);
  Multiplexer multiplexer_2 (.in0(b), .in1(not_2_out), .out(multiplexer_2_out), .sel(binvert));
  and and_1 (and_1_out, multiplexer_1_out, multiplexer_2_out);
  or or_1 (or_1_out, multiplexer_1_out, multiplexer_2_out);
  _1_bit_full_adder u_1_bit_full_adder_1 (
    .a(multiplexer_1_out), .b(multiplexer_2_out), .cin(cin), .cout(cout), .sum(n1_bit_full_adder_1_sum));
  Multiplexer #(.select(2)) multiplexer_3 (
    .in0(and_1_out), .in1(or_1_out), .in2(n1_bit_full_adder_1_sum), .in3(less), .out(result), .sel(op));
endmodule

module _4_bit_ALU (
  input  [3:0] Control,
  input  zero,
  input  [3:0] a,
  input  [3:0] b,
  output [3:0] result,
  output Zero_2,
  output Overflow
);

  wire n1_bit_alu_1_cout, n1_bit_alu_2_cout, n1_bit_alu_3_cout, n1_bit_full_adder_overflow_detect_1_set,
       or_1_out;

  _1_bit_ALU u_1_bit_alu_1 (
    .a(a[0]), .b(b[0]), .less(n1_bit_full_adder_overflow_detect_1_set), .ainvert(Control[3]),
    .binvert(Control[2]), .cin(Control[2]), .op(Control[1:0]), .cout(n1_bit_alu_1_cout), .result(result[0]));
  _1_bit_ALU u_1_bit_alu_2 (
    .a(a[1]), .b(b[1]), .less(zero), .ainvert(Control[3]), .binvert(Control[2]), .cin(n1_bit_alu_1_cout),
    .op(Control[1:0]), .cout(n1_bit_alu_2_cout), .result(result[1]));
  _1_bit_ALU u_1_bit_alu_3 (
    .a(a[2]), .b(b[2]), .less(zero), .ainvert(Control[3]), .binvert(Control[2]), .cin(n1_bit_alu_2_cout),
    .op(Control[1:0]), .cout(n1_bit_alu_3_cout), .result(result[2]));
  _1_bit_full_adder_overflow_detect u_1_bit_full_adder_overflow_detect_1 (
    .a(a[3]), .b(b[3]), .less(zero), .ainvert(Control[3]), .binvert(Control[2]), .cin(n1_bit_alu_3_cout),
    .op(Control[1:0]), .result(result[3]), .set(n1_bit_full_adder_overflow_detect_1_set), .Overflow(Overflow));
  not not_1 (Zero_2, or_1_out);
  or or_1 (or_1_out, result[0], result[1], result[2], result[3]);
endmodule

module _1_bit_full_adder_overflow_detect (
  input  ainvert,
  input  binvert,
  input  cin,
  input  [1:0] op,
  input  a,
  input  b,
  input  less,
  output result,
  output set,
  output Overflow
);

  wire and_1_out, multiplexer_1_out, multiplexer_2_out, n1_bit_full_adder_1_cout, not_1_out, not_2_out,
       or_1_out;

  Multiplexer multiplexer_1 (.in0(a), .in1(not_1_out), .out(multiplexer_1_out), .sel(ainvert));
  not not_1 (not_1_out, a);
  not not_2 (not_2_out, b);
  Multiplexer multiplexer_2 (.in0(b), .in1(not_2_out), .out(multiplexer_2_out), .sel(binvert));
  and and_1 (and_1_out, multiplexer_1_out, multiplexer_2_out);
  or or_1 (or_1_out, multiplexer_1_out, multiplexer_2_out);
  _1_bit_full_adder u_1_bit_full_adder_1 (
    .a(multiplexer_1_out), .b(multiplexer_2_out), .cin(cin), .cout(n1_bit_full_adder_1_cout), .sum(set));
  Overflow_detection overflow_detection_1 (.cin(cin), .cout(n1_bit_full_adder_1_cout), .Overflow(Overflow));
  Multiplexer #(.select(2)) multiplexer_3 (
    .in0(and_1_out), .in1(or_1_out), .in2(set), .in3(less), .out(result), .sel(op));
endmodule

module Overflow_detection (
  input  cin,
  input  cout,
  output Overflow
);

  wire and_1_out, and_2_out;

  and and_1 (and_1_out, ~cin, cout);  // AND_Gate
  and and_2 (and_2_out, cin, ~cout);  // AND_Gate
  or or_1 (Overflow, and_1_out, and_2_out);
endmodule

module CPU (
);

  wire control_1_p2;
  wire [1:0] control_1_p3;
  wire [3:0] control_1_p4;
  wire [31:0] n16_bit_sign_extender_1_out, undriven;

  // Control control_1: pin names not known; wires that end beside it: undriven[31:26], control_1_p2, control_1_p3, control_1_p4
  Multiplexer #(.width(5)) multiplexer_1 (
    .in0(undriven[20:16]), .in1(undriven[15:11]), .sel(control_1_p2));  // open: out
  _16_bit_sign_extender u_16_bit_sign_extender_1 (.in(undriven[15:0]), .out(n16_bit_sign_extender_1_out));
  ALU_Control alu_control_1 (
    .funct(undriven[5:0]), .ALUOp_in(control_1_p3), .immidiate_input(control_1_p4));  // open: ALU_input
  // RegisterFile registerfile_1: pin names not known; wires that end beside it: n16_bit_sign_extender_1_out
endmodule

module _16_bit_sign_extender (
  input  [15:0] in,
  output [31:0] out
);


  assign out = {{17{in[15]}}, in[14:0]};
endmodule

module Control (
  input  [5:0] in_1,
  output RegDst,
  output ALUSrc,
  output MemToReg,
  output RegWrite,
  output MemRead,
  output MemWrite,
  output Branch,
  output [1:0] ALUOp,
  output [3:0] immediate_ALU_instruct
);

  PLA #(.in_width(6), .out_width(9), .truth_table("000000,100100010#R-instructions\n001100,010100000#andi mangler\n001001,110100000#addiu\n001101,000000000#ori mangler\n001010,000000000#stlti mangler\n000100,000000101#beq\n101011,010001000#sw\n100011,011110000#lw")) pla_1 (.out(MemRead));  // open: in
  // PLA #(.in_width(6), .out_width(4), .truth_table("001001,0010#addiu\n001100,0000#andi\n001101,0001#ori\n001010,0111#slti")) pla_2: pin names not known; wires that end beside it: immediate_ALU_instruct
endmodule

module ALU_Control (
  input  [3:0] immidiate_input,
  input  [5:0] funct,
  input  [1:0] ALUOp_in,
  output [3:0] ALU_input
);

  wire and_1_out;
  wire [3:0] pla_1_p1;

  and and_1 (and_1_out, ~ALUOp_in[0], ALUOp_in[1]);  // AND_Gate
  // PLA #(.in_width(6), .out_width(4), .truth_table("100001,0010#addu\n100011,0110#subu\n100100,0000#and\n100101,0001#or\n101010,0111#slt")) pla_1: pin names not known; wires that end beside it: pla_1_p1
  Multiplexer #(.width(4)) multiplexer_1 (.in0(immidiate_input), .in1(pla_1_p1), .out(ALU_input), .sel(and_1_out));
endmodule

module _5_32_decoder (
  input  [4:0] in_1,
  output [31:0] out_2
);

  wire and_1_out, decoder_1_out0, decoder_1_out1, decoder_1_out2, decoder_1_out3, decoder_1_out4,
       decoder_1_out5, decoder_1_out6, decoder_1_out7, decoder_1_out8, decoder_1_out9, decoder_1_out10,
       decoder_1_out11, decoder_1_out12, decoder_1_out13, decoder_1_out14, decoder_1_out15, not_1_out;
  wire [15:0] decoder_2_out0;
  wire [31:0] n16_to_32_bit_filler_1_out;

  Decoder #(.select(4)) decoder_1 (
    .out0(decoder_1_out0), .out1(decoder_1_out1), .out2(decoder_1_out2), .out3(decoder_1_out3),
    .out4(decoder_1_out4), .out5(decoder_1_out5), .out6(decoder_1_out6), .out7(decoder_1_out7),
    .out8(decoder_1_out8), .out9(decoder_1_out9), .out10(decoder_1_out10), .out11(decoder_1_out11),
    .out12(decoder_1_out12), .out13(decoder_1_out13), .out14(decoder_1_out14), .out15(decoder_1_out15),
    .sel(in_1[3:0]));
  Decoder #(.select(4)) decoder_2 (
    .out0(decoder_2_out0[0]), .out1(decoder_2_out0[1]), .out2(decoder_2_out0[2]), .out3(decoder_2_out0[3]),
    .out4(decoder_2_out0[4]), .out5(decoder_2_out0[5]), .out6(decoder_2_out0[6]), .out7(decoder_2_out0[7]),
    .out8(decoder_2_out0[8]), .out9(decoder_2_out0[9]), .out10(decoder_2_out0[10]),
    .out11(decoder_2_out0[11]), .out12(decoder_2_out0[12]), .out13(decoder_2_out0[13]),
    .out14(decoder_2_out0[14]), .out15(decoder_2_out0[15]), .sel(in_1[3:0]));
  and and_1 (and_1_out, ~in_1[4], decoder_1_out0, decoder_1_out1, decoder_1_out2, decoder_1_out3, decoder_1_out4, decoder_1_out5, decoder_1_out6, decoder_1_out7, decoder_1_out8, decoder_1_out9, decoder_1_out10, decoder_1_out11, decoder_1_out12, decoder_1_out13, decoder_1_out14, decoder_1_out15);  // AND_Gate
  _16_to_32_bit_filler u_16_to_32_bit_filler_1 (.in(decoder_2_out0), .high(in_1[4]), .out(n16_to_32_bit_filler_1_out));
  not not_1 (not_1_out, and_1_out);
  Multiplexer #(.width(32)) multiplexer_1 (
    .in0(32'h10), .in1(n16_to_32_bit_filler_1_out), .out(out_2), .sel(not_1_out));
endmodule

module _16_to_32_bit_filler (
  input  [15:0] in,
  input  high,
  output [31:0] out
);

  Multiplexer #(.width(32)) multiplexer_1 (.in0({{16{1'b0}}, in}), .in1({in, {16{1'b0}}}), .out(out), .sel(high));
endmodule
